# Fritzing sketch Circuit Diagram (saved by Fritzing 0.9.3b)

parts:
  Mod1 = Raspberry Pi Pico
  S1 = Pushbutton [package="[THT]"]
  ENCODER1 = Rotary Encoder with Knob
  S2 = Pushbutton [package="[THT]"]
  S3 = Pushbutton [package="[THT]"]
  S4 = Pushbutton [package="[THT]"]
  S5 = Pushbutton [package="[THT]"]
  S6 = Pushbutton [package="[THT]"]
  S7 = Pushbutton [package="[THT]"]
  S8 = Pushbutton [package="[THT]"]
  S9 = Pushbutton [package="[THT]"]
  S10 = Pushbutton [package="[THT]"]
  S11 = Pushbutton [package="[THT]"]
  S12 = Pushbutton [package="[THT]"]
  S13 = Pushbutton [package="[THT]"]
  S15 = Pushbutton [package="[THT]"]
  S16 = Pushbutton [package="[THT]"]
  R1 = Resistor [tolerance=±5% resistance=10k package="1206 [SMD]"]
  R2 = Resistor [tolerance=±5% resistance=10k package="1206 [SMD]"]
  R3 = Resistor [tolerance=±5% resistance=10k package="1206 [SMD]"]
  R4 = Resistor [tolerance=±5% resistance=10k package="1206 [SMD]"]
  R1_2 = Resistor [tolerance=±5% resistance=10k package="1206 [SMD]"]
  R5 = Resistor [tolerance=±5% resistance=10k package="1206 [SMD]"]
  R6 = Resistor [tolerance=±5% resistance=10k package="1206 [SMD]"]

nets:
  N1: Mod1.pin_15, ENCODER1.no_name_yet#1, R6.Pin_1
  N2: Mod1.pin_16, ENCODER1.no_name_yet#3, R5.Pin_1
  N3: Mod1.pin_17, ENCODER1.no_name_yet#4
  N4: Mod1.pin_18, Mod1.pin_38, Mod1.pin_42, ENCODER1.no_name_yet#2, ENCODER1.no_name_yet#5, R1.Pin_1, R2.Pin_1, R3.Pin_1, R4.Pin_1, R1_2.Pin_1
  N5: Mod1.pin_22, S1.Pin_3, S1.Pin_4, S2.Pin_3, S2.Pin_4, S3.Pin_3, S3.Pin_4, R1.Pin_0
  N6: Mod1.pin_24, S4.Pin_3, S4.Pin_4, S5.Pin_3, S5.Pin_4, S6.Pin_3, S6.Pin_4, R2.Pin_0
  N7: Mod1.pin_25, S7.Pin_3, S7.Pin_4, S8.Pin_3, S8.Pin_4, S9.Pin_3, S9.Pin_4, R3.Pin_0
  N8: Mod1.pin_26, S11.Pin_3, S11.Pin_4, S13.Pin_3, S13.Pin_4, S15.Pin_3, S15.Pin_4, R1_2.Pin_0
  N9: Mod1.pin_27, S10.Pin_3, S10.Pin_4, S12.Pin_3, S12.Pin_4, S16.Pin_3, S16.Pin_4, R4.Pin_0
  N10: Mod1.pin_29, S1.Pin_1, S1.Pin_2, S6.Pin_1, S6.Pin_2, S9.Pin_1, S9.Pin_2, S10.Pin_1, S10.Pin_2, S13.Pin_1, S13.Pin_2
  N11: Mod1.pin_31, Mod1.pin_32, S2.Pin_1, S2.Pin_2, S3.Pin_1, S3.Pin_2, S4.Pin_1, S4.Pin_2, S5.Pin_1, S5.Pin_2, S7.Pin_1, S7.Pin_2, S8.Pin_1, S8.Pin_2, S11.Pin_1, S11.Pin_2, S12.Pin_1, S12.Pin_2, S15.Pin_1, S15.Pin_2, S16.Pin_1, S16.Pin_2
  N12: Mod1.pin_36, R5.Pin_0, R6.Pin_0

custom parts:
  Raspberry Pi Pico: Raspberry Pi Pico. Based around the RP2040 microcontroller the Pico is a low cost microcontroller device bringing Raspberry Pi quality, cost, and easy of use to the microcontroller space. Jan 2021, Split part in to two versions: tht (this one) and SMD. This one will drill holes for a .1 in header in pcb to allow plugging in the module as well as providing pads to solder the module to the top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
  Rotary Encoder with Knob: Rotary Encoder with 1/4" Shaft and Knob
